// Logisim project atividade ula.circ as structural Verilog: 3 circuits, main circuit main
module main (
);

  HalfAdder halfadder_1 ();  // open: X, Y, S, CarryOut
  FullAdder fulladder_1 ();  // open: CarryIn, X, Y, S, CarryOut
endmodule

module HalfAdder (
  input  X,
  input  Y,
  output S,
  output CarryOut
);

  xor xor_1 (S, X, Y);
  and and_1 (CarryOut, X, Y);
endmodule

module FullAdder (
  input  CarryIn,
  input  X,
  input  Y,
  output S,
  output CarryOut
);

  wire halfadder_1_carryout, halfadder_1_s, halfadder_2_carryout;

  HalfAdder halfadder_1 (.X(X), .Y(Y), .S(halfadder_1_s), .CarryOut(halfadder_1_carryout));
  HalfAdder halfadder_2 (.X(CarryIn), .Y(halfadder_1_s), .S(S), .CarryOut(halfadder_2_carryout));
  or or_1 (CarryOut, halfadder_2_carryout, halfadder_1_carryout);
endmodule
